# Fritzing sketch blink-led (saved by Fritzing 0.9.3b)
breadboards: 1

parts:
  R1 = Resistor [tolerance=±5% resistance=330 package=THT]
  LED1 = LED - 5mm [color="Red (633nm)" package="5 mm [THT]"]
  Part1 = Arduino Uno (Rev3)

nets:
  N1: R1.Pin_0, Part1.D13/SCK
  N2: R1.Pin_1, LED1.cathode
  N3: LED1.anode, Part1.GND

// code stored in the sketch: blink-led.ino
#define LED 13  // The pin the LED is connected to
void setup() {
  pinMode(LED, OUTPUT); // Declare the LED as an output
}

void loop() {
  digitalWrite(LED, HIGH); // Turn the LED on
  delay(1000);
  digitalWrite(LED, LOW);
  delay(1000);
}
